// Logisim project bfcpu.circ as structural Verilog: 4 circuits, main circuit main
module main (
);

  wire and_1_out, button_1_out, controller_1_fdec, controller_1_halted, controller_1_rclk, controller_1_wclk,
       demultiplexer_1_out0, demultiplexer_1_out1, demultiplexer_1_out2, demultiplexer_1_out3, not_1_out,
       or_1_out;
  wire [1:0] controller_1_cycle, controller_1_seloperand;
  wire [3:0] rom_1_data;
  wire [6:0] keyboard_1_data;
  wire [7:0] alu_1_res, alu_1_res_2, controlled_buffer_2_out, controller_1_counter, ram_1_data;
  wire [15:0] alu_1_tsto_out, DP_q, multiplexer_1_out, PC_q;

  Button button_1 (.out(button_1_out));
  Keyboard #(.buflen(32), .trigger("rising")) keyboard_1 (
    .clk(button_1_out), .data(keyboard_1_data));  // open: re, clr, avail
  // Buffer buffer_1 is placed but not wired
  Register #(.width(16), .trigger("rising")) PC (
    .D({alu_1_res_2, alu_1_res}), .Q(PC_q), .clk(demultiplexer_1_out1));  // open: en, clr
  // Probe on {{9{1'b0}}, keyboard_1_data}
  ROM #(.addrWidth(16), .dataWidth(4)) rom_1 (.addr(PC_q), .data(rom_1_data));  // open: sel
  Demultiplexer #(.select(2), .width(1), .tristate("false")) demultiplexer_1 (
    .out0(demultiplexer_1_out0), .out1(demultiplexer_1_out1), .out2(demultiplexer_1_out2),
    .out3(demultiplexer_1_out3), .in(controller_1_wclk), .sel(controller_1_seloperand));
  // Probe on rom_1_data
  // Probe on button_1_out
  or or_1 (or_1_out, demultiplexer_1_out0, demultiplexer_1_out3);
  // Probe on controller_1_rclk
  // Probe on controller_1_wclk
  Controller controller_1 (
    .Opcode(rom_1_data), .Halt(button_1_out), .WCLK(controller_1_wclk), .RCLK(controller_1_rclk),
    .Halted(controller_1_halted), .Counter(controller_1_counter), .Cycle(controller_1_cycle),
    .selOperand(controller_1_seloperand), .fDec(controller_1_fdec));
  // Probe on controller_1_cycle
  // Probe on controller_1_counter
  LED #(.active("true")) Halted (.in(controller_1_halted));
  Register #(.width(16), .trigger("rising")) DP (
    .D({alu_1_res_2, alu_1_res}), .Q(DP_q), .clk(demultiplexer_1_out2));  // open: en, clr
  // Probe on controller_1_seloperand
  and and_1 (and_1_out, or_1_out, controller_1_wclk);
  not not_1 (not_1_out, and_1_out);
  // Probe on multiplexer_1_out
  // Probe on alu_1_tsto_out
  Multiplexer #(.select(2), .width(16)) multiplexer_1 (
    .in0({{9{1'b0}}, keyboard_1_data}), .in1(PC_q), .in2(DP_q), .in3({{8{1'b0}}, controlled_buffer_2_out}),
    .out(multiplexer_1_out), .sel(controller_1_seloperand));
  // Probe on controller_1_fdec
  RAM #(.addrWidth(16), .dataWidth(8), .bus("asynch")) ram_1 (
    .addr(DP_q), .data(ram_1_data), .ld(not_1_out));  // open: sel, clr
  assign ram_1_data = and_1_out ? alu_1_res : 8'bz;  // Controlled_Buffer controlled_buffer_1
  assign controlled_buffer_2_out = not_1_out ? ram_1_data : 8'bz;  // Controlled_Buffer controlled_buffer_2
  // Probe on controlled_buffer_2_out
  ALU alu_1 (
    .PAR(multiplexer_1_out), .ART_PAR(controller_1_fdec), .OP(2'b00), .TSTO_OUT(alu_1_tsto_out),
    .clk(controller_1_rclk), .RES({alu_1_res_2, alu_1_res}));  // open: NZ
  // Probe on {alu_1_res_2, alu_1_res}

  // Notes on the sheet:
  //   INPUT DRIVER
  //   PROGRAM ROM
  //   contents of rom_1 (hex, n*v repeats v):
  //   0 2 0 2
  //   CONTROL UNIT
  //   DATA RAM
endmodule

module ALU (
  input  [15:0] PAR,
  input  ART_PAR,
  input  clk,
  input  [1:0] OP,
  output [15:0] TSTO_OUT,
  output NZ,
  output [15:0] RES
);

  wire adder_1_cout, adder_2_cout, adder_3_cout, or_1_out, or_2_out;
  wire [3:0] adder_1_out, adder_2_out, adder_3_out, adder_4_out;

  or or_1 (or_1_out, 1'b0, PAR[0], PAR[1], PAR[2], PAR[3], PAR[4], PAR[5], PAR[6], PAR[7]);
  or or_2 (or_2_out, 1'b0, PAR[8], PAR[9], PAR[10], PAR[11], PAR[12], PAR[13], PAR[14], PAR[15]);
  or or_3 (NZ, or_1_out, or_2_out);
  Adder #(.width(4)) adder_1 (
    .a(PAR[3:0]), .b({{3{ART_PAR}}, 1'b1}), .out(adder_1_out), .cin(1'b0), .cout(adder_1_cout));
  Adder #(.width(4)) adder_2 (
    .a(PAR[7:4]), .b({4{ART_PAR}}), .out(adder_2_out), .cin(adder_1_cout), .cout(adder_2_cout));
  Adder #(.width(4)) adder_3 (
    .a(PAR[11:8]), .b({4{ART_PAR}}), .out(adder_3_out), .cin(adder_2_cout), .cout(adder_3_cout));
  Adder #(.width(4)) adder_4 (.a(PAR[15:12]), .b({4{ART_PAR}}), .out(adder_4_out), .cin(adder_3_cout));  // open: cout
  Multiplexer #(.select(2), .width(16)) multiplexer_1 (
    .in0({adder_4_out, adder_3_out, adder_2_out, adder_1_out}), .in1(PAR), .in2({PAR[7:0], PAR[15:8]}),
    .in3({RES[15:8], PAR[7:0]}), .out(TSTO_OUT), .sel(OP));
  Register #(.width(16), .trigger("rising")) BUF (.D(TSTO_OUT), .Q(RES), .clk(clk));  // open: en, clr
endmodule

module xx (
  input  [7:0] D,
  input  en,
  input  clk,
  output [7:0] Q
);

  wire [7:0] multiplexer_1_out;

  Multiplexer #(.select(1), .width(8)) multiplexer_1 (.in0(Q), .in1(D), .out(multiplexer_1_out), .sel(en));
  Register #(.width(8), .trigger("rising")) register_1 (.D(multiplexer_1_out), .Q(Q), .clk(clk));  // open: en, clr
endmodule

module Controller (
  input  [3:0] Opcode,
  input  Halt,
  output WCLK,
  output RCLK,
  output [1:0] selOperand,
  output fDec,
  output Halted,
  output [7:0] Counter,
  output [1:0] Cycle
);

  wire and_1_out, and_2_out, and_3_out, clock_1_out, d_ff_1_qn, decoder_1_out0, decoder_1_out1,
       decoder_2_out0, demultiplexer_1_out0, demultiplexer_1_out1, multiplexer_1_out, not_1_out, not_2_out,
       not_3_out, not_4_out, or_1_out, t_ff_1_qn, xnor_1_out;
  wire [2:2] multiplexer_2_out;

  T_Flip_Flop #(.trigger("rising")) t_ff_1 (
    .clk(multiplexer_1_out), .T(1'b1), .Q(Halted), .Qn(t_ff_1_qn));  // open: preset, reset, en
  Multiplexer #(.select(1), .width(1)) multiplexer_1 (
    .in0(decoder_2_out0), .in1(Halt), .out(multiplexer_1_out), .sel(Halted));
  Clock #(.highDuration(1), .lowDuration(1)) clock_1 (.out(clock_1_out));
  and and_1 (and_1_out, clock_1_out, t_ff_1_qn);
  not not_1 (not_1_out, clock_1_out);
  and and_2 (and_2_out, decoder_2_out0, not_2_out);
  not not_2 (not_2_out, and_3_out);
  and and_3 (and_3_out, or_1_out, not_3_out);
  not not_3 (not_3_out, d_ff_1_qn);
  D_Flip_Flop #(.trigger("rising")) d_ff_1 (
    .clk(not_1_out), .D(and_2_out), .Qn(d_ff_1_qn));  // open: Q, preset, en, reset
  Demultiplexer #(.select(1), .width(1), .tristate("false")) demultiplexer_1 (
    .out0(demultiplexer_1_out0), .out1(demultiplexer_1_out1), .in(and_1_out), .sel(d_ff_1_qn));
  not not_4 (not_4_out, or_1_out);
  or or_1 (or_1_out, demultiplexer_1_out0, demultiplexer_1_out1);
  Counter #(.width(2), .max('h3), .ongoal("wrap"), .trigger("rising")) counter_1 (
    .Q(Cycle), .clk(demultiplexer_1_out1));  // open: load, D, count, carry, clr
  and and_4 (RCLK, not_4_out, decoder_1_out1);
  and and_5 (WCLK, not_4_out, decoder_1_out0);
  Decoder #(.select(1), .tristate("false")) decoder_1 (.out0(decoder_1_out0), .out1(decoder_1_out1), .sel(Cycle[0]));
  xnor xnor_1 (xnor_1_out, Cycle[0], Cycle[1]);
  Multiplexer #(.select(1), .width(4)) multiplexer_2 (
    .in0(Opcode), .in1(4'b0001), .out({fDec, multiplexer_2_out[2], selOperand}), .sel(xnor_1_out));
  Decoder #(.select(2), .tristate("false")) decoder_2 (
    .out0(decoder_2_out0), .sel(selOperand));  // open: out1, out2, out3
  // Probe on selOperand
  Counter #(.width(8), .max('hff), .ongoal("wrap"), .trigger("rising")) counter_2 (
    .Q(Counter), .clk(demultiplexer_1_out1));  // open: load, D, count, carry, clr
endmodule
